// Logisim project gmux.circ as structural Verilog: 1 circuit, main circuit main
module main (
  input  in_1,
  input  in_2,
  output \and ,
  output \or ,
  output \xor ,
  output \not 
);

  Multiplexer #(.select(2), .disabled(0), .enable("false")) multiplexer_1 (
    .in0(1'b0), .in1(1'b0), .in2(1'b0), .in3(1'b1), .out(\and ), .sel({in_1, in_2}));
  Multiplexer #(.select(2), .disabled(0), .enable("false")) multiplexer_2 (
    .in0(1'b0), .in1(1'b1), .in2(1'b1), .in3(1'b1), .out(\or ), .sel({in_1, in_2}));
  Multiplexer #(.select(2), .disabled(0), .enable("false")) multiplexer_3 (
    .in0(1'b0), .in1(1'b1), .in2(1'b1), .in3(1'b0), .out(\xor ), .sel({in_1, in_2}));
  Multiplexer #(.disabled(0), .enable("false")) multiplexer_4 (.in0(1'b1), .in1(1'b0), .out(\not ), .sel(in_2));
endmodule
