// Logisim project register_file.circ as structural Verilog: 1 circuit, main circuit main
module main (
  input  [2:0] R1,
  input  [2:0] R2,
  input  RE,
  input  [7:0] WD,
  input  WE,
  input  [2:0] WA,
  input  Reset,
  input  En,
  output [7:0] O1,
  output [7:0] O2
);

  wire and_1_out, clock_1_out, demultiplexer_2_out0, demultiplexer_2_out1, demultiplexer_2_out2,
       demultiplexer_2_out3, demultiplexer_2_out4, demultiplexer_2_out5, demultiplexer_2_out6,
       demultiplexer_2_out7;
  wire [7:0] _1_q, _2_q, _3_q, _4_q, _5_q, _6_q, _7_q, _8_q, demultiplexer_1_out0, demultiplexer_1_out1,
       demultiplexer_1_out2, demultiplexer_1_out3, demultiplexer_1_out4, demultiplexer_1_out5,
       demultiplexer_1_out6, demultiplexer_1_out7;

  Demultiplexer #(.select(3), .width(8)) demultiplexer_1 (
    .out0(demultiplexer_1_out0), .out1(demultiplexer_1_out1), .out2(demultiplexer_1_out2),
    .out3(demultiplexer_1_out3), .out4(demultiplexer_1_out4), .out5(demultiplexer_1_out5),
    .out6(demultiplexer_1_out6), .out7(demultiplexer_1_out7), .in(WD), .sel(WA), .en(WE));
  Demultiplexer #(.select(3)) demultiplexer_2 (
    .out0(demultiplexer_2_out0), .out1(demultiplexer_2_out1), .out2(demultiplexer_2_out2),
    .out3(demultiplexer_2_out3), .out4(demultiplexer_2_out4), .out5(demultiplexer_2_out5),
    .out6(demultiplexer_2_out6), .out7(demultiplexer_2_out7), .in(WE), .sel(WA), .en(WE));
  and and_1 (and_1_out, En, clock_1_out);
  Register _1 (.D(demultiplexer_1_out0), .en(demultiplexer_2_out0), .Q(_1_q), .clk(and_1_out), .clr(Reset));
  Register _2 (.D(demultiplexer_1_out1), .en(demultiplexer_2_out1), .Q(_2_q), .clk(and_1_out), .clr(Reset));
  Register _3 (.D(demultiplexer_1_out2), .en(demultiplexer_2_out2), .Q(_3_q), .clk(and_1_out), .clr(Reset));
  Register _4 (.D(demultiplexer_1_out3), .en(demultiplexer_2_out3), .Q(_4_q), .clk(and_1_out), .clr(Reset));
  Register _5 (.D(demultiplexer_1_out4), .en(demultiplexer_2_out4), .Q(_5_q), .clk(and_1_out), .clr(Reset));
  Register _6 (.D(demultiplexer_1_out5), .en(demultiplexer_2_out5), .Q(_6_q), .clk(and_1_out), .clr(Reset));
  Register _7 (.D(demultiplexer_1_out6), .en(demultiplexer_2_out6), .Q(_7_q), .clk(and_1_out), .clr(Reset));
  Register _8 (.D(demultiplexer_1_out7), .en(demultiplexer_2_out7), .Q(_8_q), .clk(and_1_out), .clr(Reset));
  Clock clock_1 (.out(clock_1_out));
  Multiplexer #(.select(3), .width(8)) multiplexer_1 (
    .in0(_1_q), .in1(_2_q), .in2(_3_q), .in3(_4_q), .in4(_5_q), .in5(_6_q), .in6(_7_q), .in7(_8_q), .out(O1),
    .sel(R1), .en(RE));
  Multiplexer #(.select(3), .width(8)) multiplexer_2 (
    .in0(_1_q), .in1(_2_q), .in2(_3_q), .in3(_4_q), .in4(_5_q), .in5(_6_q), .in6(_7_q), .in7(_8_q), .out(O2),
    .sel(R2), .en(RE));
endmodule
