// Logisim project bitwise_ops.circ as structural Verilog: 1 circuit, main circuit main
module main (
  input  [3:0] A,
  input  [3:0] B,
  input  Tri_state,
  input  [1:0] SELECT,
  output [3:0] Output
);

  wire [3:0] main_1_out_3, main_2_out_3, main_3_out_2, main_4_out_4, multiplexer_1_out;

  bitwise_xor_main main_1 (.A(A), .B(B), .out_3(main_1_out_3));
  bitwise_and_main main_2 (.A(A), .B(B), .out_3(main_2_out_3));
  bit_complement_main main_3 (.A(A), .out_2(main_3_out_2));
  ripple_adder_main main_4 (.A(A), .B(B), .out_4(main_4_out_4));  // open: in_1, out_5
  Multiplexer #(.select(2), .width(4)) multiplexer_1 (
    .in0(main_1_out_3), .in1(main_2_out_3), .in2(main_3_out_2), .in3(main_4_out_4), .out(multiplexer_1_out),
    .sel(SELECT));  // open: en
  assign Output = Tri_state ? multiplexer_1_out : 4'bz;  // Controlled_Buffer controlled_buffer_1
endmodule
