// Logisim project Adder and subtractor.circ as structural Verilog: 1 circuit, main circuit main
module main (
  input  [3:0] A,
  input  [3:0] B,
  input  A_S,
  output [3:0] out_4,
  output overflow,
  output out_6
);

  wire adder_1_cout, adder_2_cout, adder_3_cout;
  wire [3:0] multiplexer_1_out, xor_1_out;

  Multiplexer #(.width(4), .enable("false")) multiplexer_1 (
    .in0(4'b0000), .in1(4'b1111), .out(multiplexer_1_out), .sel(A_S));
  assign xor_1_out = B ^ multiplexer_1_out;  // XOR_Gate xor_1, 4 bits wide
  Adder #(.width(1)) adder_1 (.a(A[0]), .b(xor_1_out[0]), .out(out_4[0]), .cin(A_S), .cout(adder_1_cout));
  Adder #(.width(1)) adder_2 (.a(A[1]), .b(xor_1_out[1]), .out(out_4[1]), .cin(adder_1_cout), .cout(adder_2_cout));
  Adder #(.width(1)) adder_3 (.a(A[2]), .b(xor_1_out[2]), .out(out_4[2]), .cin(adder_2_cout), .cout(adder_3_cout));
  Adder #(.width(1)) adder_4 (.a(A[3]), .b(xor_1_out[3]), .out(out_4[3]), .cin(adder_3_cout), .cout(out_6));
  xor xor_2 (overflow, adder_3_cout, out_6);
endmodule
