// Logisim project bit-complement.circ as structural Verilog: 1 circuit, main circuit main
module main (
  input  [3:0] A,
  output [3:0] out_2
);

  assign out_2 = ~A;  // NOT_Gate not_1, 4 bits wide
endmodule
