// Logisim project ring_counter.circ as structural Verilog: 1 circuit, main circuit main
module main (
  input  Enable,
  input  Reset,
  output [3:0] Value
);

  wire clock_1_out, xnor_1_out;

  Clock clock_1 (.out(clock_1_out));
  D_Flip_Flop d_ff_1 (.clk(clock_1_out), .D(xnor_1_out), .Q(Value[3]), .en(Enable), .reset(Reset));  // open: Qn, preset
  D_Flip_Flop d_ff_2 (.clk(clock_1_out), .D(Value[3]), .Q(Value[2]), .en(Enable), .reset(Reset));  // open: Qn, preset
  NotExactlyOne xnor_1 (.out(xnor_1_out), .in0(Value[3]), .in1(Value[2]), .in2(Value[1]), .in3(Value[0]));
  D_Flip_Flop d_ff_3 (.clk(clock_1_out), .D(Value[2]), .Q(Value[1]), .en(Enable), .reset(Reset));  // open: Qn, preset
  D_Flip_Flop d_ff_4 (.clk(clock_1_out), .D(Value[1]), .Q(Value[0]), .en(Enable), .reset(Reset));  // open: Qn, preset
endmodule
