// Logisim project arm_pc.circ as structural Verilog: 1 circuit, main circuit main
module main (
  input  cp,
  input  clr
);

  wire clock_1_out;
  wire [31:0] counter_1_q, shifter_1_out;

  Clock clock_1 (.out(clock_1_out));
  Shifter #(.width(32)) shifter_1 (.in(counter_1_q), .\dist (5'b00010), .out(shifter_1_out));
  Counter #(.width(32), .max('h3fffffff), .ongoal("stay")) counter_1 (
    .count(cp), .Q(counter_1_q), .clk(clock_1_out), .clr(clr));  // open: load, D, carry
  Hex_Digit_Display hex_digit_display_1 (.value(shifter_1_out[3:0]));  // open: dp
  Hex_Digit_Display hex_digit_display_2 (.value(shifter_1_out[7:4]));  // open: dp
  Hex_Digit_Display hex_digit_display_3 (.value(shifter_1_out[11:8]));  // open: dp
  Hex_Digit_Display hex_digit_display_4 (.value(shifter_1_out[15:12]));  // open: dp
  Hex_Digit_Display hex_digit_display_5 (.value(shifter_1_out[19:16]));  // open: dp
  Hex_Digit_Display hex_digit_display_6 (.value(shifter_1_out[23:20]));  // open: dp
  Hex_Digit_Display hex_digit_display_7 (.value(shifter_1_out[27:24]));  // open: dp
  Hex_Digit_Display hex_digit_display_8 (.value(shifter_1_out[31:28]));  // open: dp
endmodule
