// Logisim project full_adder.circ as structural Verilog: 1 circuit, main circuit main
module main (
  input  a0,
  input  a1,
  input  c,
  output s,
  output c_2
);

  wire and_1_out, and_2_out, xor_1_out;

  xor xor_1 (xor_1_out, a0, a1);
  and and_1 (and_1_out, c, xor_1_out);
  and and_2 (and_2_out, a1, a0);
  xor xor_2 (s, xor_1_out, c);
  or or_1 (c_2, and_1_out, and_2_out);
endmodule
