// Logisim project pc.circ as structural Verilog: 1 circuit, main circuit main
// Program Counter
module main (
  input  cp,
  input  clr,
  input  Ep
);

  wire and_1_out, and_2_out, and_3_out, and_4_out, clk_out, t_ff_1_q, t_ff_2_q, t_ff_3_q, t_ff_4_q;

  Clock clk (.out(clk_out));
  LED led_1 (.in(and_1_out));
  and and_1 (and_1_out, Ep, t_ff_1_q);
  T_Flip_Flop #(.trigger("falling")) t_ff_1 (.clk(clk_out), .T(cp), .Q(t_ff_1_q), .reset(clr));  // open: Qn, preset, en
  and and_2 (and_2_out, Ep, t_ff_2_q);
  T_Flip_Flop #(.trigger("falling")) t_ff_2 (
    .clk(t_ff_1_q), .T(1'b1), .Q(t_ff_2_q), .reset(clr));  // open: Qn, preset, en
  LED led_2 (.in(and_2_out));
  LED led_3 (.in(and_3_out));
  and and_3 (and_3_out, Ep, t_ff_3_q);
  T_Flip_Flop #(.trigger("falling")) t_ff_3 (
    .clk(t_ff_2_q), .T(1'b1), .Q(t_ff_3_q), .reset(clr));  // open: Qn, preset, en
  and and_4 (and_4_out, Ep, t_ff_4_q);
  T_Flip_Flop #(.trigger("falling")) t_ff_4 (
    .clk(t_ff_3_q), .T(1'b1), .Q(t_ff_4_q), .reset(clr));  // open: Qn, preset, en
  LED led_4 (.in(and_4_out));
endmodule
