// Logisim project pclib.circ as structural Verilog: 1 circuit, main circuit main
// Program Counter
module main (
  input  clk,
  input  cp,
  input  clr,
  input  Ep,
  output pc0,
  output pc1,
  output pc2,
  output pc3
);

  wire t_ff_1_q, t_ff_2_q, t_ff_3_q, t_ff_4_q;

  and and_1 (pc0, Ep, t_ff_1_q);
  T_Flip_Flop #(.trigger("falling")) t_ff_1 (.clk(clk), .T(cp), .Q(t_ff_1_q), .reset(clr));  // open: Qn, preset, en
  and and_2 (pc1, Ep, t_ff_2_q);
  T_Flip_Flop #(.trigger("falling")) t_ff_2 (
    .clk(t_ff_1_q), .T(1'b1), .Q(t_ff_2_q), .reset(clr));  // open: Qn, preset, en
  and and_3 (pc2, Ep, t_ff_3_q);
  T_Flip_Flop #(.trigger("falling")) t_ff_3 (
    .clk(t_ff_2_q), .T(1'b1), .Q(t_ff_3_q), .reset(clr));  // open: Qn, preset, en
  and and_4 (pc3, Ep, t_ff_4_q);
  T_Flip_Flop #(.trigger("falling")) t_ff_4 (
    .clk(t_ff_3_q), .T(1'b1), .Q(t_ff_4_q), .reset(clr));  // open: Qn, preset, en
endmodule
