// Logisim project ripple_adder.circ as structural Verilog: 1 circuit, main circuit main
module main (
  input  in_1,
  input  [3:0] A,
  input  [3:0] B,
  output [3:0] out_4,
  output out_5
);

  wire adder_1_cout, adder_2_cout, adder_3_cout;

  Adder #(.width(1)) adder_1 (.a(A[0]), .b(B[0]), .out(out_4[0]), .cin(in_1), .cout(adder_1_cout));
  Adder #(.width(1)) adder_2 (.a(A[1]), .b(B[1]), .out(out_4[1]), .cin(adder_1_cout), .cout(adder_2_cout));
  Adder #(.width(1)) adder_3 (.a(A[2]), .b(B[2]), .out(out_4[2]), .cin(adder_2_cout), .cout(adder_3_cout));
  Adder #(.width(1)) adder_4 (.a(A[3]), .b(B[3]), .out(out_4[3]), .cin(adder_3_cout), .cout(out_5));
endmodule
